// Logisim project Lab5_var1.circ as structural Verilog: 1 circuit, main circuit main
module main (
  input  V,
  input  Reset,
  input  in_3,
  output q3_prime,
  output out_5,
  output q2_prime,
  output out_7,
  output q1_prime,
  output out_9
);

  wire and_1_out, and_2_out;

  D_Flip_Flop d_ff_1 (.clk(in_3));  // open: D, Q, Qn, preset, en, reset
  and and_1 (and_1_out, V, q1_prime, q2_prime);
  and and_2 (and_2_out, V, q1_prime);
  T_Flip_Flop t_ff_1 ();  // open: clk, T, Q, Qn, preset, reset, en
  // T_flip_flop_with_reset t_flip_flop_with_reset_1: pin names not known; wires that end beside it: and_1_out, Reset, q3_prime, out_5
  // T_flip_flop_with_reset t_flip_flop_with_reset_2: pin names not known; wires that end beside it: and_2_out, Reset, q2_prime, out_7
  // T_flip_flop_with_reset t_flip_flop_with_reset_3: pin names not known; wires that end beside it: V, Reset, q1_prime, out_9
  J_K_Flip_Flop j_k_ff_1 ();  // open: J, clk, K, Q, Qn, preset, en, reset
  S_R_Flip_Flop s_r_ff_1 ();  // open: S, clk, R, Q, Qn, preset, reset, en
  Hex_Digit_Display hex_digit_display_1 (.value({1'b0, q3_prime, q2_prime, q1_prime}));  // open: dp

  // Notes on the sheet:
  //   h1=V
  //   h3
  //   h2
  //   h1
  //   h2=q1'*V
  //   h3=q1'*q2'V
  //   q3
  //   q2
  //   q1
  //   q1=!h1*q1(i-1) + h1*!q1(i-1)
  //   q2=!h2*q2(i-1) + h2*!q2(i-1)
  //   q3=!h3*q3(i-1) + h3*!q3(i-1)
  //   q1'=!h1*q1+h1*!q1
  //   q2'=!h2*q2+h2*!q2
  //   q3'=!h3*q3+h3*!q3
endmodule
