// Logisim project log_4_2.circ as structural Verilog
module dgd (
  input  a,
  input  b,
  input  c,
  output d,
  output b_2
);

  wire and_1_out, and_2_out, and_3_out, and_4_out, and_5_out, and_6_out, and_7_out, not_1_out, not_2_out,
       not_3_out, not_4_out, not_5_out, not_6_out, not_7_out, not_8_out;

  not not_1 (not_1_out, a);
  not not_2 (not_2_out, b);
  not not_3 (not_3_out, a);
  not not_4 (not_4_out, c);
  not not_5 (not_5_out, b);
  not not_6 (not_6_out, c);
  not not_7 (not_7_out, a);
  not not_8 (not_8_out, a);
  and and_1 (and_1_out, not_1_out, not_2_out, c);
  and and_2 (and_2_out, not_3_out, b, not_4_out);
  and and_3 (and_3_out, a, not_5_out, not_6_out);
  and and_4 (and_4_out, a, b, c);
  and and_5 (and_5_out, not_7_out, c);
  and and_6 (and_6_out, not_8_out, b);
  and and_7 (and_7_out, b, c);
  or or_1 (d, and_1_out, and_2_out, and_3_out, and_4_out);
  or or_2 (b_2, and_5_out, and_6_out, and_7_out);
endmodule

module dng (
  input  a,
  input  b,
  input  c,
  input  d,
  output a1,
  output b1,
  output c1,
  output d1
);

  wire and_1_out, and_2_out, and_3_out, and_4_out, and_5_out, and_6_out, and_7_out, and_8_out, and_9_out,
       and_10_out, and_11_out, and_12_out, and_13_out, not_1_out, not_2_out, not_3_out, not_4_out, not_5_out,
       not_6_out, not_7_out, not_8_out, not_9_out, not_10_out, not_11_out, not_12_out, not_13_out,
       not_14_out, not_15_out, not_16_out, not_17_out, not_18_out, not_19_out, not_20_out, not_21_out,
       not_22_out, not_23_out;

  not not_1 (not_1_out, a);
  and and_1 (and_1_out, not_1_out, b);
  not not_2 (not_2_out, a);
  and and_2 (and_2_out, not_2_out, c, d);
  and and_3 (and_3_out, a, not_3_out, not_4_out);
  not not_3 (not_3_out, b);
  not not_4 (not_4_out, c);
  and and_4 (and_4_out, a, not_5_out, not_6_out);
  not not_5 (not_5_out, b);
  not not_6 (not_6_out, d);
  not not_7 (not_7_out, b);
  not not_8 (not_8_out, d);
  not not_9 (not_9_out, b);
  not not_10 (not_10_out, c);
  not not_11 (not_11_out, a);
  not not_12 (not_12_out, a);
  not not_13 (not_13_out, c);
  and and_5 (and_5_out, not_12_out, not_13_out, d);
  not not_14 (not_14_out, b);
  and and_6 (and_6_out, not_14_out, not_15_out, d);
  not not_15 (not_15_out, c);
  not not_16 (not_16_out, a);
  and and_7 (and_7_out, not_16_out, c, not_17_out);
  not not_17 (not_17_out, d);
  not not_18 (not_18_out, b);
  and and_8 (and_8_out, not_18_out, c, not_19_out);
  not not_19 (not_19_out, d);
  not not_20 (not_20_out, b);
  and and_9 (and_9_out, not_20_out, not_21_out);
  not not_21 (not_21_out, d);
  not not_22 (not_22_out, a);
  and and_10 (and_10_out, not_22_out, not_23_out);
  not not_23 (not_23_out, d);
  or or_1 (a1, and_1_out, and_2_out, and_3_out, and_4_out);
  and and_11 (and_11_out, not_7_out, not_8_out);
  and and_12 (and_12_out, not_9_out, not_10_out);
  or or_2 (b1, and_11_out, and_12_out, and_13_out);
  and and_13 (and_13_out, not_11_out, b, c, d);
  or or_3 (c1, and_5_out, and_6_out, and_7_out, and_8_out);
  or or_4 (d1, and_9_out, and_10_out);
endmodule
